# Fritzing sketch StaffTrainer (saved by Fritzing 1.0.2b)
perfboards: 4

parts:
  S1 = Pushbutton [package="[THT]"]
  S2 = Pushbutton [package="[THT]"]
  S3 = Pushbutton [package="[THT]"]
  S4 = Pushbutton [package="[THT]"]
  S5 = Pushbutton [package="[THT]"]
  S6 = Pushbutton [package="[THT]"]
  S7 = Pushbutton [package="[THT]"]
  S8 = Pushbutton [package="[THT]"]
  S9 = Pushbutton [package="[THT]"]
  S10 = Pushbutton [package="[THT]"]
  S11 = Pushbutton [package="[THT]"]
  S12 = Pushbutton [package="[THT]"]
  U1 = LuaNode32 / ESP32 [part_number=ESP32S-PIN30]
  SG1 = Buzzer 12mm [part_number=COM-07950 package=buzzer-12mm-ns]
  R2 = 6mm Trimmer Potentiometer [maximum_resistance=10kΩ knob_status=50% power=0.5W package=THT]
  VCC1 = Battery  # not connected
  VCC2 = Battery  # not connected
  S13 = Taiway 100-SP-X-T1 SPDT Miniature Toggle Switch [part_number=100-SP-X-T1-0-0-B1-M1 package=THT]
  U2 = mystery part, 7 pins [chip_label=LCD mn=fdsf mpn=fdfs part_number=fdsaf]
  JP2 = Header 12 [package=1x12_machine-pin-header_lock.004]
  JP3 = Header 12 [package=1x12_machine-pin-header_lock.004]  # not connected
  U3 = LuaNode32 / ESP32 [part_number=ESP32S-PIN30]  # not connected
  S14 = Pushbutton [package="[THT]"]  # not connected
  S15 = Pushbutton [package="[THT]"]  # not connected
  S16 = Pushbutton [package="[THT]"]  # not connected
  S17 = Pushbutton [package="[THT]"]  # not connected
  S18 = Pushbutton [package="[THT]"]  # not connected
  S19 = Pushbutton [package="[THT]"]  # not connected
  S20 = Pushbutton [package="[THT]"]  # not connected
  S21 = Pushbutton [package="[THT]"]  # not connected
  S22 = Pushbutton [package="[THT]"]  # not connected
  S23 = Pushbutton [package="[THT]"]  # not connected
  S24 = Pushbutton [package="[THT]"]  # not connected
  S25 = Pushbutton [package="[THT]"]  # not connected
  JP4 = Header 12 [package=1x12_machine-pin-header_lock.004]  # not connected
  U4 = mystery part, 7 pins [chip_label=LCD mn=fdsf mpn=fdfs part_number=fdsaf]  # not connected
  R3 = 6mm Trimmer Potentiometer [maximum_resistance=10kΩ knob_status=50% power=0.5W package=THT]  # not connected
  R4 = 6mm Trimmer Potentiometer [maximum_resistance=10kΩ knob_status=50% power=0.5W package=THT]  # not connected
  SG2 = Buzzer 12mm [part_number=COM-07950 package=buzzer-12mm-ns]  # not connected
  VCC3 = Battery  # not connected
  VCC4 = Battery  # not connected

nets:
  N1: S1.Pin_1, S1.Pin_2, JP2.8
  N2: S1.Pin_3, S1.Pin_4, S3.Pin_3, S3.Pin_4, S4.Pin_3, S4.Pin_4, S5.Pin_3, S5.Pin_4, S6.Pin_3, S6.Pin_4, S9.Pin_3, S9.Pin_4, S10.Pin_3, S10.Pin_4, S11.Pin_3, S11.Pin_4, S12.Pin_3, S12.Pin_4, U1.GND, U2.pin6
  N3: S2.Pin_1, S2.Pin_2, JP2.9
  N4: S2.Pin_3, S2.Pin_4
  N5: S3.Pin_1, S3.Pin_2, JP2.10
  N6: S4.Pin_1, S4.Pin_2, JP2.11
  N7: S5.Pin_1, S5.Pin_2, JP2.12
  N8: S6.Pin_1, S6.Pin_2, JP2.6
  N9: S7.Pin_1, S7.Pin_2, JP2.7
  N10: S7.Pin_3, S7.Pin_4
  N11: S8.Pin_1, S8.Pin_2, JP2.3
  N12: S8.Pin_3, S8.Pin_4
  N13: S9.Pin_1, S9.Pin_2, JP2.2
  N14: S10.Pin_1, S10.Pin_2, JP2.4
  N15: S11.Pin_1, S11.Pin_2, JP2.5
  N16: S12.Pin_1, S12.Pin_2, JP2.1
  N17: U1.Vin, S13.L2
  N18: U1.3V3, U2.pin7
  N19: U1.D2, U2.pin3
  N20: U1.D4, U2.pin2
  N21: U1.TX2, SG1.1
  N22: U1.D18, U2.pin5
  N23: U1.D23, U2.pin4
  N24: SG1.2, R2.wiper

custom parts:
  LuaNode32 / ESP32: New Image for LuaNode32 DOIT ESP32 DEVKIT V1. Base parts from LuaNode32 / ESP32 ESP32 based LuaNode32 by G.Noorlander DOIT Esp32 DevKit v1 (30 pins long, 11 pins width) by Werner Rothschopf (modified by vanepp Dec 2018)
  Buzzer 12mm: Buzzer 12mm Spark Fun Electronics SKU : Comp-Buzzer Through hole This is a small 12mm round speaker that operates around the audible 2kHz range. You can use these speakers to create simple music or user interfaces. This is not a true piezoelectric speaker but behaves similarly. Instead of a piezoelectric crystal that vibrates with an electric current, this tiny speaker uses an electromagnet to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
